# Fritzing sketch esuqematico servo sharp (saved by Fritzing 0.8.3b)
breadboards: 1

parts:
  Parte1 = Arduino Uno (Rev3)
  J1 = Basic Servo
  J2 = Infrared Proximity Sensor

nets:
  N1: Parte1.A1, J2.Vout
  VCC: Parte1.5V, J1.vcc, J2.Vcc
  GND: Parte1.GND, J1.gnd, J2.GND
  N2: Parte1.D9_PWM, J1.pulse
